// Logisim project ColemanHW2Extra.circ as structural Verilog: 5 circuits, main circuit main
module main (
  input  Control_Line
);

  wire n7decode_1_d0, n7decode_1_d1, n7decode_1_d2, n7decode_1_d3, n7decode_1_d4, n7decode_1_d5,
       n7decode_1_d6, n7decode_2_d0, n7decode_2_d1, n7decode_2_d2, n7decode_2_d3, n7decode_2_d4,
       n7decode_2_d5, n7decode_2_d6, Reset_out, updgt_1_cz, updgt_1_qq0, updgt_1_qq1, updgt_1_qq2,
       updgt_1_qq3, updgt_2_qq0, updgt_2_qq1, updgt_2_qq2, updgt_2_qq3;

  Button Reset (.out(Reset_out));
  Updgt updgt_1 (
    .Control_Line(Control_Line), .Reset(Reset_out), .CZ(updgt_1_cz), .QQ3(updgt_1_qq3), .QQ2(updgt_1_qq2),
    .QQ1(updgt_1_qq1), .QQ0(updgt_1_qq0));
  Updgt updgt_2 (
    .Control_Line(updgt_1_cz), .Reset(Reset_out), .QQ3(updgt_2_qq3), .QQ2(updgt_2_qq2), .QQ1(updgt_2_qq1),
    .QQ0(updgt_2_qq0));  // open: CZ
  _7Decode u_7decode_1 (
    .Q3(updgt_1_qq3), .Q2(updgt_1_qq2), .Q1(updgt_1_qq1), .Q0(updgt_1_qq0), .D6(n7decode_1_d6),
    .D5(n7decode_1_d5), .D4(n7decode_1_d4), .D3(n7decode_1_d3), .D2(n7decode_1_d2), .D1(n7decode_1_d1),
    .D0(n7decode_1_d0));
  _7Decode u_7decode_2 (
    .Q3(updgt_2_qq3), .Q2(updgt_2_qq2), .Q1(updgt_2_qq1), .Q0(updgt_2_qq0), .D6(n7decode_2_d6),
    .D5(n7decode_2_d5), .D4(n7decode_2_d4), .D3(n7decode_2_d3), .D2(n7decode_2_d2), .D1(n7decode_2_d1),
    .D0(n7decode_2_d0));
  _7_Segment_Display u_7_segment_display_1 (
    .g(n7decode_1_d0), .f(n7decode_1_d1), .a(n7decode_1_d2), .b(n7decode_1_d3), .e(n7decode_1_d4),
    .d(n7decode_1_d5), .c(n7decode_1_d6));  // open: dp
  _7_Segment_Display u_7_segment_display_2 (
    .g(n7decode_2_d0), .f(n7decode_2_d1), .a(n7decode_2_d2), .b(n7decode_2_d3), .e(n7decode_2_d4),
    .d(n7decode_2_d5), .c(n7decode_2_d6));  // open: dp
endmodule

module Flops (
  input  DD3,
  input  DD2,
  input  DD1,
  input  DD0,
  input  Clkx,
  input  Reset,
  output QQ3,
  output QQ2,
  output QQ1,
  output QQ0
);

  D_Flip_Flop d_ff_1 (.clk(Clkx), .D(DD3), .Q(QQ3), .reset(Reset));  // open: Qn, preset, en
  D_Flip_Flop d_ff_2 (.clk(Clkx), .D(DD2), .Q(QQ2), .reset(Reset));  // open: Qn, preset, en
  D_Flip_Flop d_ff_3 (.clk(Clkx), .D(DD1), .Q(QQ1), .reset(Reset));  // open: Qn, preset, en
  D_Flip_Flop d_ff_4 (.clk(Clkx), .D(DD0), .Q(QQ0), .reset(Reset));  // open: Qn, preset, en
endmodule

module Updgt_comb (
  input  Q3,
  input  Q2,
  input  Q1,
  input  Q0,
  input  CX,
  output D3,
  output D2,
  output D1,
  output D0,
  output CZ
);

  wire and_1_out, and_2_out, and_3_out, and_4_out, and_5_out, and_6_out, and_7_out, and_8_out, and_9_out,
       and_10_out, and_11_out, and_12_out, and_13_out, and_14_out, not_1_out, not_2_out, not_3_out,
       not_4_out, not_5_out, not_6_out, not_7_out, not_8_out, not_9_out, not_10_out, not_11_out, not_12_out,
       not_13_out, not_14_out, not_15_out, not_16_out, not_17_out, not_18_out, not_19_out, not_20_out,
       not_21_out, not_22_out, not_23_out, not_24_out, not_25_out, not_26_out, not_27_out, not_28_out,
       not_29_out, not_30_out, not_31_out, not_32_out, not_33_out;

  not not_1 (not_1_out, Q3);
  not not_2 (not_2_out, Q2);
  not not_3 (not_3_out, Q1);
  not not_4 (not_4_out, Q0);
  not not_5 (not_5_out, Q2);
  not not_6 (not_6_out, Q1);
  not not_7 (not_7_out, CX);
  not not_8 (not_8_out, Q3);
  not not_9 (not_9_out, Q2);
  not not_10 (not_10_out, Q3);
  not not_11 (not_11_out, Q1);
  not not_12 (not_12_out, Q3);
  not not_13 (not_13_out, Q0);
  not not_14 (not_14_out, Q3);
  not not_15 (not_15_out, CX);
  not not_16 (not_16_out, Q3);
  not not_17 (not_17_out, Q1);
  not not_18 (not_18_out, Q3);
  not not_19 (not_19_out, Q0);
  not not_20 (not_20_out, Q3);
  not not_21 (not_21_out, CX);
  not not_22 (not_22_out, Q3);
  not not_23 (not_23_out, Q0);
  not not_24 (not_24_out, Q2);
  not not_25 (not_25_out, Q1);
  not not_26 (not_26_out, Q0);
  not not_27 (not_27_out, Q3);
  not not_28 (not_28_out, CX);
  not not_29 (not_29_out, Q2);
  not not_30 (not_30_out, Q1);
  not not_31 (not_31_out, CX);
  not not_32 (not_32_out, Q2);
  not not_33 (not_33_out, Q1);
  and and_1 (and_1_out, not_1_out, Q2, Q1, Q0, CX);
  and and_2 (and_2_out, Q3, not_2_out, not_3_out, not_4_out);
  and and_3 (and_3_out, Q3, not_5_out, not_6_out, not_7_out);
  and and_4 (and_4_out, not_8_out, not_9_out, Q1, Q0, CX);
  and and_5 (and_5_out, not_10_out, Q2, not_11_out);
  and and_6 (and_6_out, not_12_out, Q2, not_13_out);
  and and_7 (and_7_out, not_14_out, Q2, not_15_out);
  and and_8 (and_8_out, not_16_out, not_17_out, Q0, CX);
  and and_9 (and_9_out, not_18_out, Q1, not_19_out);
  and and_10 (and_10_out, not_20_out, Q1, not_21_out);
  and and_11 (and_11_out, not_22_out, not_23_out, CX);
  and and_12 (and_12_out, not_24_out, not_25_out, not_26_out, CX);
  and and_13 (and_13_out, not_27_out, Q0, not_28_out);
  and and_14 (and_14_out, not_29_out, not_30_out, Q0, not_31_out);
  and and_15 (CZ, Q3, not_32_out, not_33_out, Q0, CX);
  or or_1 (D3, and_1_out, and_2_out, and_3_out);
  or or_2 (D2, and_4_out, and_5_out, and_6_out, and_7_out);
  or or_3 (D1, and_8_out, and_9_out, and_10_out);
  or or_4 (D0, and_11_out, and_12_out, and_13_out, and_14_out);
endmodule

module Updgt (
  input  Reset,
  input  Control_Line,
  output QQ3,
  output QQ2,
  output QQ1,
  output QQ0,
  output CZ
);

  wire clock_1_out, updgt_comb_1_d0, updgt_comb_1_d1, updgt_comb_1_d2, updgt_comb_1_d3;

  Updgt_comb updgt_comb_1 (
    .Q3(QQ3), .Q2(QQ2), .Q1(QQ1), .Q0(QQ0), .CX(Control_Line), .D3(updgt_comb_1_d3), .D2(updgt_comb_1_d2),
    .D1(updgt_comb_1_d1), .D0(updgt_comb_1_d0), .CZ(CZ));
  Clock clock_1 (.out(clock_1_out));
  Flops flops_1 (
    .DD3(updgt_comb_1_d3), .DD2(updgt_comb_1_d2), .DD1(updgt_comb_1_d1), .DD0(updgt_comb_1_d0),
    .Clkx(clock_1_out), .Reset(Reset), .QQ3(QQ3), .QQ2(QQ2), .QQ1(QQ1), .QQ0(QQ0));
endmodule

module _7Decode (
  input  Q3,
  input  Q2,
  input  Q1,
  input  Q0,
  output D6,
  output D5,
  output D4,
  output D3,
  output D2,
  output D1,
  output D0
);

  wire and_1_out, and_2_out, and_3_out, and_4_out, and_5_out, and_6_out, and_7_out, and_8_out, and_9_out,
       and_10_out, and_11_out, and_12_out, and_13_out, and_14_out, and_15_out, and_16_out, and_17_out,
       and_18_out, and_19_out, and_20_out, and_21_out, and_22_out, and_23_out, and_24_out, and_25_out,
       and_26_out, not_1_out, not_2_out, not_3_out, not_4_out, not_5_out, not_6_out, not_7_out, not_8_out,
       not_9_out, not_10_out, not_11_out, not_12_out, not_13_out, not_14_out, not_15_out, not_16_out,
       not_17_out, not_18_out, not_19_out, not_20_out, not_21_out, not_22_out, not_23_out, not_24_out,
       not_25_out, not_26_out, not_27_out, not_28_out, not_29_out, not_30_out, not_31_out, not_32_out,
       not_33_out, not_34_out, not_35_out, not_36_out, not_37_out, not_38_out, not_39_out, not_40_out,
       not_41_out, not_42_out, not_43_out, not_44_out, not_45_out, not_46_out, not_47_out, not_48_out,
       not_49_out, not_50_out, not_51_out, not_52_out;

  not not_1 (not_1_out, Q2);
  and and_1 (and_1_out, not_1_out, not_2_out);
  not not_2 (not_2_out, Q1);
  not not_3 (not_3_out, Q3);
  and and_2 (and_2_out, not_3_out, Q0);
  not not_4 (not_4_out, Q3);
  and and_3 (and_3_out, not_4_out, Q2);
  not not_5 (not_5_out, Q3);
  not not_6 (not_6_out, Q2);
  not not_7 (not_7_out, Q0);
  not not_8 (not_8_out, Q3);
  not not_9 (not_9_out, Q2);
  not not_10 (not_10_out, Q3);
  not not_11 (not_11_out, Q0);
  not not_12 (not_12_out, Q3);
  not not_13 (not_13_out, Q1);
  not not_14 (not_14_out, Q2);
  not not_15 (not_15_out, Q1);
  not not_16 (not_16_out, Q2);
  not not_17 (not_17_out, Q1);
  and and_4 (and_4_out, not_16_out, not_17_out, not_18_out);
  not not_18 (not_18_out, Q0);
  not not_19 (not_19_out, Q3);
  and and_5 (and_5_out, not_19_out, Q1, not_20_out);
  not not_20 (not_20_out, Q0);
  not not_21 (not_21_out, Q3);
  and and_6 (and_6_out, not_21_out, not_22_out);
  not not_22 (not_22_out, Q2);
  not not_23 (not_23_out, Q3);
  not not_24 (not_24_out, Q1);
  and and_7 (and_7_out, not_23_out, not_24_out, not_25_out);
  not not_25 (not_25_out, Q0);
  not not_26 (not_26_out, Q2);
  and and_8 (and_8_out, not_26_out, not_27_out);
  not not_27 (not_27_out, Q1);
  not not_28 (not_28_out, Q3);
  and and_9 (and_9_out, not_28_out, Q1, Q0);
  not not_29 (not_29_out, Q3);
  not not_30 (not_30_out, Q2);
  and and_10 (and_10_out, not_29_out, not_30_out, not_31_out);
  not not_31 (not_31_out, Q0);
  not not_32 (not_32_out, Q3);
  and and_11 (and_11_out, not_32_out, Q1);
  not not_33 (not_33_out, Q3);
  and and_12 (and_12_out, not_33_out, Q2, Q0);
  not not_34 (not_34_out, Q2);
  and and_13 (and_13_out, Q3, not_34_out, not_35_out);
  not not_35 (not_35_out, Q1);
  not not_36 (not_36_out, Q3);
  and and_14 (and_14_out, not_36_out, not_37_out, not_38_out);
  not not_37 (not_37_out, Q1);
  not not_38 (not_38_out, Q0);
  not not_39 (not_39_out, Q3);
  and and_15 (and_15_out, not_39_out, Q2, not_40_out);
  not not_40 (not_40_out, Q1);
  not not_41 (not_41_out, Q3);
  and and_16 (and_16_out, not_41_out, Q2, not_42_out);
  not not_42 (not_42_out, Q0);
  and and_17 (and_17_out, Q3, not_43_out, not_44_out);
  not not_43 (not_43_out, Q2);
  not not_44 (not_44_out, Q1);
  not not_45 (not_45_out, Q3);
  and and_18 (and_18_out, not_45_out, not_46_out, Q1);
  not not_46 (not_46_out, Q2);
  not not_47 (not_47_out, Q3);
  and and_19 (and_19_out, not_47_out, Q2, not_48_out);
  not not_48 (not_48_out, Q1);
  not not_49 (not_49_out, Q3);
  and and_20 (and_20_out, not_49_out, Q2, not_50_out);
  not not_50 (not_50_out, Q0);
  and and_21 (and_21_out, Q3, not_51_out, not_52_out);
  not not_51 (not_51_out, Q2);
  not not_52 (not_52_out, Q1);
  or or_1 (D6, and_1_out, and_2_out, and_3_out);
  and and_22 (and_22_out, not_5_out, not_6_out, not_7_out);
  and and_23 (and_23_out, not_8_out, not_9_out, Q1);
  and and_24 (and_24_out, not_10_out, Q1, not_11_out);
  and and_25 (and_25_out, not_12_out, Q2, not_13_out, Q0);
  and and_26 (and_26_out, Q3, not_14_out, not_15_out);
  or or_2 (D4, and_4_out, and_5_out);
  or or_3 (D3, and_6_out, and_7_out, and_8_out, and_9_out);
  or or_4 (D2, and_10_out, and_11_out, and_12_out, and_13_out);
  or or_5 (D1, and_14_out, and_15_out, and_16_out, and_17_out);
  or or_6 (D0, and_18_out, and_19_out, and_20_out, and_21_out);
  or or_7 (D5, and_22_out, and_23_out, and_24_out, and_25_out, and_26_out);
endmodule
